# Fritzing sketch 16_lightv3 (saved by Fritzing 0.9.3b)
circuit board: 12cm x 7cm
perfboards: 1

parts:
  R0 = Resistor [tolerance=±5% resistance=220 package=THT]
  R1 = Resistor [tolerance=±5% resistance=220 package=THT]
  R2 = Resistor [tolerance=±5% resistance=220 package=THT]
  R3 = Resistor [tolerance=±5% resistance=220 package=THT]
  R5 = Resistor [tolerance=±5% resistance=220 package=THT]
  R6 = Resistor [tolerance=±5% resistance=220 package=THT]
  R7 = Resistor [tolerance=±5% resistance=220 package=THT]
  LED8 = LED - 5mm [color="Red (633nm)" package="5 mm [THT]"]
  R8 = Resistor [tolerance=±5% resistance=220 package=THT]
  R9 = Resistor [tolerance=±5% resistance=220 package=THT]
  LED9 = LED - 5mm [color="Red (633nm)" package="5 mm [THT]"]
  LED10 = LED - 5mm [color="Red (633nm)" package="5 mm [THT]"]
  R10 = Resistor [tolerance=±5% resistance=220 package=THT]
  LED11 = LED - 5mm [color="Red (633nm)" package="5 mm [THT]"]
  R11 = Resistor [tolerance=±5% resistance=220 package=THT]
  LED12 = LED - 5mm [color="Red (633nm)" package="5 mm [THT]"]
  R12 = Resistor [tolerance=±5% resistance=220 package=THT]
  LED13 = LED - 5mm [color="Red (633nm)" package="5 mm [THT]"]
  R13 = Resistor [tolerance=±5% resistance=220 package=THT]
  LED14 = LED - 5mm [color="Red (633nm)" package="5 mm [THT]"]
  R14 = Resistor [tolerance=±5% resistance=220 package=THT]
  LED15 = LED - 5mm [color="Red (633nm)" package="5 mm [THT]"]
  R15 = Resistor [tolerance=±5% resistance=220 package=THT]
  R4 = Resistor [tolerance=±5% resistance=220 package=THT]
  Mod1 = Raspberry Pi Pico
  LED0 = LED - 5mm [color="Red (633nm)" package="5 mm [THT]"]
  LED1 = LED - 5mm [color="Red (633nm)" package="5 mm [THT]"]
  LED2 = LED - 5mm [color="Red (633nm)" package="5 mm [THT]"]
  LED3 = LED - 5mm [color="Red (633nm)" package="5 mm [THT]"]
  LED7 = LED - 5mm [color="Red (633nm)" package="5 mm [THT]"]
  LED4 = LED - 5mm [color="Red (633nm)" package="5 mm [THT]"]
  LED6 = LED - 5mm [color="Red (633nm)" package="5 mm [THT]"]
  LED5 = LED - 5mm [color="Red (633nm)" package="5 mm [THT]"]

nets:
  N1: R0.Pin_0, LED7.anode
  N2: R0.Pin_1, Mod1.pin_10
  N3: R1.Pin_0, LED4.anode
  N4: R1.Pin_1, Mod1.pin_6
  N5: R2.Pin_0, LED6.anode
  N6: R2.Pin_1, Mod1.pin_9
  N7: R3.Pin_0, LED5.anode
  N8: R3.Pin_1, Mod1.pin_7
  N9: R5.Pin_0, Mod1.pin_4
  N10: R5.Pin_1, LED2.anode
  N11: R6.Pin_0, LED1.anode
  N12: R6.Pin_1, Mod1.pin_2
  N13: R7.Pin_0, Mod1.pin_1
  N14: R7.Pin_1, LED0.anode
  N15: LED8.cathode, LED9.cathode, LED10.cathode, LED11.cathode, LED12.cathode, LED13.cathode, LED14.cathode, LED15.cathode, Mod1.pin_3, Mod1.pin_13, Mod1.pin_18, Mod1.pin_38, LED0.cathode, LED1.cathode, LED2.cathode, LED3.cathode, LED7.cathode, LED4.cathode, LED6.cathode, LED5.cathode
  N16: LED8.anode, R8.Pin_1
  N17: R8.Pin_0, Mod1.pin_11
  N18: R9.Pin_0, Mod1.pin_12
  N19: R9.Pin_1, LED9.anode
  N20: LED10.anode, R10.Pin_1
  N21: R10.Pin_0, Mod1.pin_14
  N22: LED11.anode, R11.Pin_1
  N23: R11.Pin_0, Mod1.pin_15
  N24: LED12.anode, R12.Pin_1
  N25: R12.Pin_0, Mod1.pin_16
  N26: LED13.anode, R13.Pin_1
  N27: R13.Pin_0, Mod1.pin_17
  N28: LED14.anode, R14.Pin_1
  N29: R14.Pin_0, Mod1.pin_19
  N30: LED15.anode, R15.Pin_1
  N31: R15.Pin_0, Mod1.pin_20
  N32: R4.Pin_0, Mod1.pin_5
  N33: R4.Pin_1, LED3.anode

custom parts:
  Raspberry Pi Pico: Raspberry Pi Pico. Based around the RP2040 microcontroller the Pico is a low cost microcontroller device bringing Raspberry Pi quality, cost, and easy of use to the microcontroller space. Jan 2021, Split part in to two versions: tht (this one) and SMD. This one will drill holes for a .1 in header in pcb to allow plugging in the module as well as providing pads to solder the module to the top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
